// Logisim project TN1.circ as structural Verilog: 1 circuit, main circuit main
module main (
  input  a,
  input  b,
  input  c,
  output out_4,
  output out_5,
  output out_6
);

  wire nand_1_out;

  nand nand_1 (nand_1_out, b, a);
  ExactlyOne xor_1 (.out(out_4), .in0(c), .in1(b), .in2(a));
  nand nand_2 (out_5, c, nand_1_out);
  nand nand_3 (out_6, c, b, a);
endmodule
