// Logisim project TN2.circ as structural Verilog: 1 circuit, main circuit main
module main (
  input  X,
  input  Y,
  input  Z,
  output _1,
  output _2,
  output _3,
  output _4,
  output _5
);

  wire and_1_out, and_2_out, not_1_out, not_2_out, not_3_out, or_1_out, or_2_out, X_prime_Y_prime_out,
       X_Y__prime_2_out, X_Y__prime_out, X_Z_out, Y_Z_out;

  not not_1 (not_1_out, X);
  not not_2 (not_2_out, Y);
  nor X_Y__prime (X_Y__prime_out, Y, X);
  and X_prime_Y_prime (X_prime_Y_prime_out, not_2_out, not_1_out);
  and Y_Z (Y_Z_out, Y, Z);
  nand X_Y__prime_2 (X_Y__prime_2_out, Y, X);
  not not_3 (not_3_out, X_Y__prime_out);
  or or_1 (or_1_out, Y_Z_out, X);
  or X_Z (X_Z_out, Z, X);
  and and_1 (and_1_out, Y, not_1_out);
  and and_2 (and_2_out, not_3_out, X_Z_out);
  or or_2 (or_2_out, and_1_out, X);
  xnor xnor_1 (_1, X_Y__prime_out, X_prime_Y_prime_out);
  xnor xnor_2 (_2, X_prime_Y_prime_out, X_Y__prime_2_out);
  xnor xnor_3 (_3, or_1_out, and_2_out);
  xnor xnor_4 (_4, or_2_out, X);
  xnor xnor_5 (_5, or_2_out, not_3_out);
endmodule
