// Logisim project TN3.circ as structural Verilog: 2 circuits, main circuit DFF_MS
module DFF_MS (
  input  D,
  output Q1,
  output Q2,
  output Q3,
  output Q2_2L,
  output Q2_2F
);

  wire A_q, clock_1_out, dlatch_2_q, dlatch_3_q, not_1_out;

  Clock clock_1 (.out(clock_1_out));
  DLatch dlatch_1 (.D(D), .E(clock_1_out), .Q(Q1));
  DLatch dlatch_2 (.D(D), .E(not_1_out), .Q(dlatch_2_q));
  not not_1 (not_1_out, clock_1_out);
  DLatch dlatch_3 (.D(D), .E(clock_1_out), .Q(dlatch_3_q));
  D_Flip_Flop d_ff_1 (.clk(clock_1_out), .D(D), .Q(Q2));  // open: Qn, preset, en, reset
  DLatch dlatch_4 (.D(dlatch_2_q), .E(clock_1_out), .Q(Q3));
  DLatch dlatch_5 (.D(dlatch_3_q), .E(clock_1_out), .Q(Q2_2L));
  D_Flip_Flop A (.clk(clock_1_out), .D(D), .Q(A_q));  // open: Qn, preset, en, reset
  D_Flip_Flop B (.clk(clock_1_out), .D(A_q), .Q(Q2_2F));  // open: Qn, preset, en, reset
endmodule

module DLatch (
  input  D,
  input  E,
  output Q
);

  Multiplexer multiplexer_1 (.in0(Q), .in1(D), .out(Q), .sel(E));  // open: en
endmodule
