// Logisim project TN4.circ as structural Verilog: 1 circuit, main circuit main
module main (
  input  A,
  input  B,
  input  C,
  input  D,
  output out_5,
  output out_6
);

  wire A_prime_B_prime_CD_out, A_prime_B_prime_CD_prime_out, A_prime_BC_prime_D_out, A_prime_BCD_out,
       AB_prime_CD_out, ABC_prime_D_out, and_1_out, and_2_out, and_3_out, and_4_out, F_can_out, F_pos_out,
       F_sop_out, not_1_out, not_2_out, not_3_out, not_4_out, or_1_out, or_2_out, or_3_out, or_4_out;

  not not_1 (not_1_out, A);
  not not_2 (not_2_out, B);
  not not_3 (not_3_out, C);
  not not_4 (not_4_out, D);
  and A_prime_B_prime_CD_prime (A_prime_B_prime_CD_prime_out, not_4_out, C, not_2_out, not_1_out);
  and A_prime_B_prime_CD (A_prime_B_prime_CD_out, D, C, not_2_out, not_1_out);
  and A_prime_BC_prime_D (A_prime_BC_prime_D_out, D, not_3_out, B, not_1_out);
  and A_prime_BCD (A_prime_BCD_out, D, C, B, not_1_out);
  and AB_prime_CD (AB_prime_CD_out, D, C, not_2_out, A);
  and ABC_prime_D (ABC_prime_D_out, D, not_3_out, B, A);
  and and_1 (and_1_out, D, not_3_out, B);
  and and_2 (and_2_out, D, C, not_2_out);
  and and_3 (and_3_out, D, C, not_1_out);
  and and_4 (and_4_out, C, not_2_out, not_1_out);
  or or_1 (or_1_out, C, B);
  or or_2 (or_2_out, D, not_2_out);
  or or_3 (or_3_out, D, not_1_out);
  or or_4 (or_4_out, not_3_out, not_2_out, not_1_out);
  or F_can (F_can_out, A_prime_B_prime_CD_prime_out, A_prime_B_prime_CD_out, A_prime_BC_prime_D_out, A_prime_BCD_out, AB_prime_CD_out, ABC_prime_D_out);
  or F_sop (F_sop_out, and_1_out, and_2_out, and_3_out, and_4_out);
  and F_pos (F_pos_out, or_1_out, or_2_out, or_3_out, or_4_out);
  xnor xnor_1 (out_5, F_can_out, F_sop_out);
  xnor xnor_2 (out_6, F_can_out, F_pos_out);
endmodule
